// Logisim project MILESTONE 2.circ as structural Verilog: 1 circuit, main circuit main
module main (
  output out_1
);

  wire AC_LD, AC_prime, and_1_out, and_2_out, and_3_out, and_5_out, and_6_out, and_7_out, and_8_out,
       and_9_out, and_10_out, and_11_out, and_12_out, and_13_out, and_14_out, and_15_out, and_17_out,
       and_18_out, and_19_out, and_20_out, and_21_out, and_22_out, and_23_out, and_24_out, and_25_out,
       and_26_out, and_28_out, and_29_out, and_30_out, and_31_out, and_32_out, and_33_out, AR_LD, B2, B5,
       bitselector_1_out, CLK, D0, D1, D2, D3, D4, D5, D6, D7, d_ff_1_q, DR_LD, I, IR_LD, MEM_READ,
       MEM_WRITE, MUX4, not_1_out, not_2_out, not_3_out, not_4_out, not_6_out, not_7_out, or_10_out, PC_INC,
       PC_LD, SC_CLR, SC_INC, T0, T2, T3, T4, T5, T6, X1, X2, X3, X4, X7;
  wire [2:0] ALU, bitselector_2_out, MUX;
  wire [3:0] SC_q;
  wire [6:0] AR_q, bit_extender_1_out, bitselector_3_out;
  wire [15:0] AC, alu_1_p5, bit_extender_2_out, DR_q, IR, IR_2_q, IR_q, PC_q, ram_1_data, TR_q;

  or or_1 (AR_LD, T0, T2);
  not not_1 (not_1_out, I);
  and and_1 (and_1_out, T5, D2);
  and and_2 (and_2_out, D5, T6);
  not not_2 (not_2_out, I);
  and and_3 (and_3_out, T5, D2);
  and and_4 (X2, D5, T6);
  and and_5 (and_5_out, T4, D4);
  not not_3 (not_3_out, I);
  Register #(.width(16)) u_IR (.D(IR), .en(IR_LD), .Q(IR_q), .clk(CLK));  // open: clr
  BitSelector #(.width(16)) bitselector_1 (.in(IR_q), .out(bitselector_1_out), .sel(4'b1111));
  Clock clock_1 (.out(CLK));
  and and_6 (and_6_out, T4, D2);
  and and_7 (and_7_out, D1, T4);
  and and_8 (and_8_out, T4, D5);
  and and_9 (and_9_out, D5, T5);
  and and_10 (and_10_out, D0, T4);
  and and_11 (and_11_out, T3, not_1_out, D7, B5);
  and and_12 (and_12_out, D5, T5);
  and and_13 (and_13_out, T5, D1);
  and and_14 (and_14_out, T5, D0);
  and and_15 (and_15_out, T4, D7, B5, not_2_out);
  and and_16 (X1, T5, D1);
  and and_17 (and_17_out, T5, D0);
  and and_18 (and_18_out, D3, T4);
  and and_19 (and_19_out, T4, D7, B5, not_3_out);
  and and_20 (and_20_out, not_3_out, T3, D7, B2);
  and and_21 (and_21_out, T4, D2);
  and and_22 (and_22_out, D1, T4);
  and and_23 (and_23_out, T4, D5);
  and and_24 (and_24_out, D0, T4);
  and and_25 (and_25_out, T4, D3);
  and and_26 (and_26_out, T4, D5);
  D_Flip_Flop u_I (.D(bitselector_1_out), .Q(I));  // open: clk, Qn, preset, en, reset
  Counter #(.width(4), .max('hf)) SC (.count(SC_INC), .Q(SC_q), .clk(CLK), .clr(d_ff_1_q));  // open: load, D, carry
  or or_2 (DR_LD, and_6_out, and_7_out, and_8_out, and_9_out, and_10_out, and_11_out);
  and and_27 (PC_LD, T4, D4);
  not not_4 (not_4_out, I);
  or or_3 (AC_LD, and_1_out, and_12_out, and_13_out, and_14_out, and_2_out, and_15_out);
  or or_4 (MEM_READ, and_21_out, and_22_out, IR_LD, and_23_out, and_24_out);
  or or_5 (MEM_WRITE, and_25_out, and_26_out);
  BitSelector #(.width(16), .group(3)) bitselector_2 (.in(IR_q), .out(bitselector_2_out), .sel(3'b100));
  Decoder #(.select(4)) decoder_1 (
    .out0(T0), .out1(IR_LD), .out2(T2), .out3(T3), .out4(T4), .out5(T5), .out6(T6), .sel(SC_q));  // open: out7, out8, out9, out10, out11, out12, out13, out14, out15, en
  and and_28 (and_28_out, not_4_out, T3, D7, AC_prime, B2);
  or or_6 (SC_CLR, and_3_out, X1, and_17_out, X2, and_18_out, and_5_out, and_19_out, and_20_out);
  not not_5 (SC_INC, SC_CLR);
  BitSelector #(.width(16), .group(7)) bitselector_3 (.in(IR_q), .out(bitselector_3_out), .sel(2'b00));
  Decoder #(.select(3)) decoder_2 (
    .out0(D0), .out1(D1), .out2(D2), .out3(D3), .out4(D4), .out5(D5), .out6(D6), .out7(D7),
    .sel(bitselector_2_out));  // open: en
  D_Flip_Flop d_ff_1 (.clk(CLK), .D(SC_CLR), .Q(d_ff_1_q));  // open: Qn, preset, en, reset
  or or_7 (PC_INC, IR_LD, and_28_out);
  and and_29 (and_29_out, D3, T4);
  not not_6 (not_6_out, I);
  and and_30 (and_30_out, D5, T5);
  Priority_Encoder priority_encoder_1 (
    .in1(X1), .in2(X2), .in3(X3), .in4(X4), .in7(X7), .out(ALU), .en_in(1'b1));  // open: in0, in5, in6, gs, en_out
  and and_31 (and_31_out, T5, D5);
  and and_32 (and_32_out, T5, D2);
  BitSelector #(.width(7)) bitselector_4 (.in(bitselector_3_out), .out(B5), .sel(3'b101));
  and and_33 (and_33_out, not_6_out, T3, D7, B5);
  Priority_Encoder priority_encoder_2 (
    .in0(MEM_READ), .in1(PC_LD), .in2(1'b0), .in3(1'b0), .in4(MUX4), .in5(T0), .in6(T2), .out(MUX),
    .en_in(1'b1));  // open: in7, gs, en_out
  or or_8 (X3, and_31_out, and_32_out);
  BitSelector #(.width(7)) bitselector_5 (.in(bitselector_3_out), .out(B2), .sel(3'b010));
  or or_9 (MUX4, and_29_out, and_33_out, and_30_out);
  not not_7 (not_7_out, I);
  and and_34 (X4, T5, D0);
  and and_35 (X7, not_7_out, T4, D7, B5);
  Bit_Extender #(.in_width(16), .out_width(7)) bit_extender_1 (.in(IR), .out(bit_extender_1_out));
  Register #(.width(7)) AR (.D(bit_extender_1_out), .en(AR_LD), .Q(AR_q), .clk(CLK));  // open: clr
  Register #(.width(16)) TR (.D(IR), .en(1'b0), .Q(TR_q), .clk(CLK));  // open: clr
  Register #(.width(16)) DR (.D(IR), .en(DR_LD), .Q(DR_q), .clk(CLK));  // open: clr
  Register #(.width(16)) u_AC (.D(alu_1_p5), .en(AC_LD), .Q(AC), .clk(CLK));  // open: clr
  or or_10 (or_10_out, AC[0], AC[1], AC[2], AC[3], AC[4], AC[5], AC[6], AC[7], AC[8], AC[9], AC[10], AC[11], AC[12], AC[13], AC[14], AC[15]);
  RAM #(.addrWidth(7), .dataWidth(16), .bus("separate")) ram_1 (
    .addr(AR_q), .din(IR), .data(ram_1_data), .str(MEM_WRITE), .clk(CLK), .ld(MEM_READ));  // open: sel, clr
  not not_8 (AC_prime, or_10_out);
  assign bit_extender_2_out = {{9{1'b0}}, AR_q};  // Bit_Extender bit_extender_2
  // ALU alu_1: pin names not known; wires that end beside it: DR_q, AC, ALU, out_1, alu_1_p5
  Counter #(.width(16), .max('hffff)) PC (
    .load(PC_LD), .D(IR), .count(PC_INC), .Q(PC_q), .clk(CLK));  // open: carry, clr
  Register #(.width(16)) IR_2 (.D(IR), .en(IR_LD), .Q(IR_2_q), .clk(CLK));  // open: clr
  Multiplexer #(.select(3), .width(16)) multiplexer_1 (
    .in0(ram_1_data), .in1(bit_extender_2_out), .in2(TR_q), .in3(DR_q), .in4(AC), .in5(PC_q), .in6(IR_2_q),
    .out(IR), .sel(MUX));  // open: in7, en

  // Other names for the same wires on the sheet: T1 = IR_LD
endmodule
